// Digital circuit comparador-16bit.dig as structural Verilog
module comparador_16bit (
  input  [15:0] A,
  input  [15:0] B,
  output gt,
  output eq,
  output lt
);

  wire and_1_out, and_2_out, comparador_1bit_1_eq, comparador_1bit_1_gt, comparador_1bit_1_lt,
       comparador_1bit_2_eq, comparador_1bit_2_gt, comparador_1bit_2_lt, comparador_2bit_cascata_1_eq,
       comparador_2bit_cascata_1_gt, comparador_2bit_cascata_1_lt, comparador_2bit_cascata_2_eq,
       comparador_2bit_cascata_2_gt, comparador_2bit_cascata_2_lt, comparador_2bit_cascata_3_eq,
       comparador_2bit_cascata_3_gt, comparador_2bit_cascata_3_lt, comparador_2bit_cascata_4_eq,
       comparador_2bit_cascata_4_gt, comparador_2bit_cascata_4_lt, comparador_2bit_cascata_5_eq,
       comparador_2bit_cascata_5_gt, comparador_2bit_cascata_5_lt, comparador_2bit_cascata_6_eq,
       comparador_2bit_cascata_6_gt, comparador_2bit_cascata_6_lt, comparador_2bit_cascata_7_eq,
       comparador_2bit_cascata_7_gt, comparador_2bit_cascata_7_lt;

  comparador_1bit comparador_1bit_1 (
    .A(A[14]), .B(B[14]), .gt(comparador_1bit_1_gt), .eq(comparador_1bit_1_eq), .lt(comparador_1bit_1_lt));
  comparador_2bit_cascata comparador_2bit_cascata_1 (
    .A(A[13:12]), .B(B[13:12]), .gt__In(comparador_1bit_1_gt), .eq__In(comparador_1bit_1_eq),
    .lt__In(comparador_1bit_1_lt), .gt(comparador_2bit_cascata_1_gt), .eq(comparador_2bit_cascata_1_eq),
    .lt(comparador_2bit_cascata_1_lt));
  comparador_2bit_cascata comparador_2bit_cascata_2 (
    .A(A[11:10]), .B(B[11:10]), .gt__In(comparador_2bit_cascata_1_gt), .eq__In(comparador_2bit_cascata_1_eq),
    .lt__In(comparador_2bit_cascata_1_lt), .gt(comparador_2bit_cascata_2_gt),
    .eq(comparador_2bit_cascata_2_eq), .lt(comparador_2bit_cascata_2_lt));
  comparador_1bit comparador_1bit_2 (
    .A(B[15]), .B(A[15]), .gt(comparador_1bit_2_gt), .eq(comparador_1bit_2_eq), .lt(comparador_1bit_2_lt));
  comparador_2bit_cascata comparador_2bit_cascata_3 (
    .A(A[9:8]), .B(B[9:8]), .gt__In(comparador_2bit_cascata_2_gt), .eq__In(comparador_2bit_cascata_2_eq),
    .lt__In(comparador_2bit_cascata_2_lt), .gt(comparador_2bit_cascata_3_gt),
    .eq(comparador_2bit_cascata_3_eq), .lt(comparador_2bit_cascata_3_lt));
  comparador_2bit_cascata comparador_2bit_cascata_4 (
    .A(A[7:6]), .B(B[7:6]), .gt__In(comparador_2bit_cascata_3_gt), .eq__In(comparador_2bit_cascata_3_eq),
    .lt__In(comparador_2bit_cascata_3_lt), .gt(comparador_2bit_cascata_4_gt),
    .eq(comparador_2bit_cascata_4_eq), .lt(comparador_2bit_cascata_4_lt));
  comparador_2bit_cascata comparador_2bit_cascata_5 (
    .A(A[5:4]), .B(B[5:4]), .gt__In(comparador_2bit_cascata_4_gt), .eq__In(comparador_2bit_cascata_4_eq),
    .lt__In(comparador_2bit_cascata_4_lt), .gt(comparador_2bit_cascata_5_gt),
    .eq(comparador_2bit_cascata_5_eq), .lt(comparador_2bit_cascata_5_lt));
  comparador_2bit_cascata comparador_2bit_cascata_6 (
    .A(A[3:2]), .B(B[3:2]), .gt__In(comparador_2bit_cascata_5_gt), .eq__In(comparador_2bit_cascata_5_eq),
    .lt__In(comparador_2bit_cascata_5_lt), .gt(comparador_2bit_cascata_6_gt),
    .eq(comparador_2bit_cascata_6_eq), .lt(comparador_2bit_cascata_6_lt));
  comparador_2bit_cascata comparador_2bit_cascata_7 (
    .A(A[1:0]), .B(B[1:0]), .gt__In(comparador_2bit_cascata_6_gt), .eq__In(comparador_2bit_cascata_6_eq),
    .lt__In(comparador_2bit_cascata_6_lt), .gt(comparador_2bit_cascata_7_gt),
    .eq(comparador_2bit_cascata_7_eq), .lt(comparador_2bit_cascata_7_lt));
  and and_1 (and_1_out, comparador_1bit_2_eq, comparador_2bit_cascata_7_gt);
  or or_1 (gt, comparador_1bit_2_gt, and_1_out);
  and and_2 (and_2_out, comparador_2bit_cascata_7_lt, comparador_1bit_2_eq);
  and and_3 (eq, comparador_1bit_2_eq, comparador_2bit_cascata_7_eq);
  or or_2 (lt, comparador_1bit_2_lt, and_2_out);
endmodule
