// Digital circuit comparador-1bit.dig as structural Verilog
module comparador_1bit (
  input  A,
  input  B,
  output gt,
  output eq,
  output lt
);

  and and_1 (gt, ~B, A);  // And
  and and_2 (lt, ~A, B);  // And
  xnor xnor_1 (eq, A, B);
endmodule
