// Digital circuit comparador-2bit-cascata.dig as structural Verilog
module comparador_2bit_cascata (
  input  [1:0] A,
  input  [1:0] B,
  input  gt__In,
  input  eq__In,
  input  lt__In,
  output gt,
  output eq,
  output lt
);

  wire and_1_out, and_2_out, comparador_2bit_1_eq, comparador_2bit_1_gt, comparador_2bit_1_lt;

  comparador_2bit comparador_2bit_1 (
    .A(A), .B(B), .gt(comparador_2bit_1_gt), .eq(comparador_2bit_1_eq), .lt(comparador_2bit_1_lt));
  and and_1 (and_1_out, eq__In, comparador_2bit_1_gt);
  and and_2 (and_2_out, comparador_2bit_1_lt, eq__In);
  or or_1 (gt, and_1_out, gt__In);
  and and_3 (eq, eq__In, comparador_2bit_1_eq);
  or or_2 (lt, lt__In, and_2_out);
endmodule
