// Digital circuit comparador-2bit.dig as structural Verilog
module comparador_2bit (
  input  [1:0] A,
  input  [1:0] B,
  output gt,
  output eq,
  output lt
);

  wire and_1_out, and_2_out, comparador_1bit_1_eq, comparador_1bit_1_gt, comparador_1bit_1_lt,
       comparador_1bit_2_eq, comparador_1bit_2_gt, comparador_1bit_2_lt;

  comparador_1bit comparador_1bit_1 (
    .A(A[1]), .B(B[1]), .gt(comparador_1bit_1_gt), .eq(comparador_1bit_1_eq), .lt(comparador_1bit_1_lt));
  comparador_1bit comparador_1bit_2 (
    .A(A[0]), .B(B[0]), .gt(comparador_1bit_2_gt), .eq(comparador_1bit_2_eq), .lt(comparador_1bit_2_lt));
  and and_1 (and_1_out, comparador_1bit_1_eq, comparador_1bit_2_gt);
  and and_2 (and_2_out, comparador_1bit_2_lt, comparador_1bit_1_eq);
  or or_1 (gt, and_1_out, comparador_1bit_1_gt);
  and and_3 (eq, comparador_1bit_1_eq, comparador_1bit_2_eq);
  or or_2 (lt, comparador_1bit_1_lt, and_2_out);
endmodule
