// Digital circuit somador-16bit.dig as structural Verilog
module somador_16bit (
  input  [15:0] A,
  input  [15:0] B,
  input  CI,
  output [15:0] R,
  output CO
);

  wire somador_1_co, somador_2_co, somador_3_co, somador_4_co, somador_5_co, somador_6_co, somador_7_co,
       somador_8_co, somador_9_co, somador_10_co, somador_11_co, somador_12_co, somador_13_co, somador_14_co,
       somador_15_co;

  somador somador_1 (.CI(CI), .A(A[0]), .B(B[0]), .R(R[0]), .CO(somador_1_co));
  somador somador_2 (.CI(somador_1_co), .A(A[1]), .B(B[1]), .R(R[1]), .CO(somador_2_co));
  somador somador_3 (.CI(somador_2_co), .A(A[2]), .B(B[2]), .R(R[2]), .CO(somador_3_co));
  somador somador_4 (.CI(somador_3_co), .A(A[3]), .B(B[3]), .R(R[3]), .CO(somador_4_co));
  somador somador_5 (.CI(somador_4_co), .A(A[4]), .B(B[4]), .R(R[4]), .CO(somador_5_co));
  somador somador_6 (.CI(somador_5_co), .A(A[5]), .B(B[5]), .R(R[5]), .CO(somador_6_co));
  somador somador_7 (.CI(somador_6_co), .A(A[6]), .B(B[6]), .R(R[6]), .CO(somador_7_co));
  somador somador_8 (.CI(somador_7_co), .A(A[7]), .B(B[7]), .R(R[7]), .CO(somador_8_co));
  somador somador_9 (.CI(somador_8_co), .A(A[8]), .B(B[8]), .R(R[8]), .CO(somador_9_co));
  somador somador_10 (.CI(somador_9_co), .A(A[9]), .B(B[9]), .R(R[9]), .CO(somador_10_co));
  somador somador_11 (.CI(somador_10_co), .A(A[10]), .B(B[10]), .R(R[10]), .CO(somador_11_co));
  somador somador_12 (.CI(somador_11_co), .A(A[11]), .B(B[11]), .R(R[11]), .CO(somador_12_co));
  somador somador_13 (.CI(somador_12_co), .A(A[12]), .B(B[12]), .R(R[12]), .CO(somador_13_co));
  somador somador_14 (.CI(somador_13_co), .A(A[13]), .B(B[13]), .R(R[13]), .CO(somador_14_co));
  somador somador_15 (.CI(somador_14_co), .A(A[14]), .B(B[14]), .R(R[14]), .CO(somador_15_co));
  somador somador_16 (.CI(somador_15_co), .A(A[15]), .B(B[15]), .R(R[15]), .CO(CO));
endmodule
