// Digital circuit somador.dig as structural Verilog
module somador (
  input  CI,
  input  A,
  input  B,
  output R,
  output CO
);

  wire and_1_out, and_2_out, or_1_out;

  and and_1 (and_1_out, A, B);
  or or_1 (or_1_out, A, B);
  xor xor_1 (R, CI, A, B);
  and and_2 (and_2_out, or_1_out, CI);
  or or_2 (CO, and_1_out, and_2_out);
endmodule
