// Digital circuit ula.dig as structural Verilog
module ula (
  input  [15:0] A,
  input  [15:0] B,
  input  [2:0] Func,
  output [15:0] R,
  output Zero
);

  wire comparador_16bit_1_eq, comparador_16bit_1_gt, comparador_16bit_1_lt, multiplexer_1_out;
  wire [15:0] and_1_out, bitextender_1_out, bitextender_2_out, bitextender_3_out, multiplexer_2_out,
       not_1_out, not_2_out, or_1_out, somador_16bit_1_r;

  comparador_16bit comparador_16bit_1 (
    .A(A), .B(B), .gt(comparador_16bit_1_gt), .eq(comparador_16bit_1_eq), .lt(comparador_16bit_1_lt));
  Multiplexer #(.Selector_Bits(3)) multiplexer_1 (
    .sel(Func), .in_0(1'b0), .in_1(1'b1), .in_2(1'b0), .in_3(1'b0), .in_4(1'b0), .in_5(1'b0), .in_6(1'b0),
    .in_7(1'b0), .out(multiplexer_1_out));
  assign and_1_out = A & B;  // And and_1, 16 bits wide
  assign or_1_out = A | B;  // Or or_1, 16 bits wide
  BitExtender #(.inputBits(1)) bitextender_1 (.in(comparador_16bit_1_eq), .out(bitextender_1_out));
  BitExtender #(.inputBits(1)) bitextender_2 (.in(comparador_16bit_1_gt), .out(bitextender_2_out));
  BitExtender #(.inputBits(1)) bitextender_3 (.in(comparador_16bit_1_lt), .out(bitextender_3_out));
  assign not_1_out = ~A;  // Not not_1, 16 bits wide
  Multiplexer #(.Selector_Bits(3), .Bits(16)) multiplexer_2 (
    .sel(Func), .in_0(B), .in_1(not_2_out), .in_2(B), .in_3(B), .in_4(B), .in_5(B), .in_6(B), .in_7(B),
    .out(multiplexer_2_out));
  somador_16bit somador_16bit_1 (
    .A(A), .B(multiplexer_2_out), .CI(multiplexer_1_out), .R(somador_16bit_1_r));  // open: CO
  Multiplexer #(.Selector_Bits(3), .Bits(16)) multiplexer_3 (
    .sel(Func), .in_0(somador_16bit_1_r), .in_1(somador_16bit_1_r), .in_2(and_1_out), .in_3(or_1_out),
    .in_4(not_1_out), .in_5(bitextender_1_out), .in_6(bitextender_2_out), .in_7(bitextender_3_out), .out(R));
  assign not_2_out = ~B;  // Not not_2, 16 bits wide
  comparador_16bit comparador_16bit_2 (.A({16{1'b0}}), .B(R), .eq(Zero));  // open: gt, lt
endmodule
